# Fritzing sketch incubator (saved by Fritzing 0.9.2b)
perfboards: 1

parts:
  J1_Peltier = Peltier Element
  F1_Fan_12VDC = Fan - Ventilador [package=THT]
  12VDC_in = 2.1mm Barrel Jack with Terminal Block
  BeagleBone1 = BeagleBone Black V3
  S2 = H-Bridge with L298N v2
  5VDC_out_to_BeagleBone = 2.1mm Barrel Jack with Terminal Block
  R16 = Resistor [tolerance=±5% resistance=4.7k package=THT]
  R17 = Resistor [tolerance=±5% resistance=2.0k package=THT]
  C16 = Electrolytic Capacitor [capacitance=10µF package="100 mil [THT, electrolytic]"]
  100k_Therm1 = Temperature Sensor (Thermistor) [thermistor_type=NTC package=THT]
  R19 = Resistor [tolerance=±5% resistance=4.7k package=THT]
  R20 = Resistor [tolerance=±5% resistance=2.0k package=THT]
  C17 = Electrolytic Capacitor [capacitance=10µF package="100 mil [THT, electrolytic]"]
  100k_Therm2 = Temperature Sensor (Thermistor) [thermistor_type=NTC package=THT]
  R22 = Resistor [tolerance=±5% resistance=4.7k package=THT]
  R23 = Resistor [tolerance=±5% resistance=2.0k package=THT]
  C19 = Electrolytic Capacitor [capacitance=10µF package="100 mil [THT, electrolytic]"]
  100k_Therm3 = Temperature Sensor (Thermistor) [thermistor_type=NTC package=THT]
  C23 = Ceramic Capacitor [capacitance=100nF voltage=20V package="100 mil [THT, multilayer]"]
  C24 = Ceramic Capacitor [capacitance=100nF package="100 mil [THT, multilayer]"]
  C25 = Ceramic Capacitor [capacitance=100nF package="100 mil [THT, multilayer]"]

nets:
  N1: J1_Peltier.pin1, S2.OUT2
  N2: J1_Peltier.pin2, S2.OUT1
  N3: F1_Fan_12VDC.5V, S2.OUT4
  N4: F1_Fan_12VDC.GND, S2.OUT3
  N5: 12VDC_in.POS, S2.+VS
  N6: 12VDC_in.NEG, S2.GND, 5VDC_out_to_BeagleBone.NEG
  N7: BeagleBone1.P9.31, R17.Pin_1, R20.Pin_1, R23.Pin_1
  N8: BeagleBone1.P9.33, C16.-, 100k_Therm1.pin_0, C17.-, 100k_Therm2.pin_0, C19.-, 100k_Therm3.pin_0, C23.0, C24.0, C25.0
  N9: BeagleBone1.P9.35, R16.Pin_1, C16.+, C24.1
  N10: BeagleBone1.P9.37, R19.Pin_1, C17.+, C23.1
  N11: BeagleBone1.P9.39, R22.Pin_1, C19.+, C25.1
  N12: BeagleBone1.P8.08, S2.ENA
  N13: BeagleBone1.P8.10, S2.IN1
  N14: BeagleBone1.P8.12, S2.IN2
  N15: BeagleBone1.P8.14, S2.IN3
  N16: BeagleBone1.P8.16, S2.IN4
  N17: BeagleBone1.P8.18, S2.ENB
  N18: S2.+VSS, 5VDC_out_to_BeagleBone.POS
  N19: R16.Pin_0, R17.Pin_0, 100k_Therm1.pin_1
  N20: R19.Pin_0, R20.Pin_0, 100k_Therm2.pin_1
  N21: R22.Pin_0, R23.Pin_0, 100k_Therm3.pin_1

custom parts:
  Fan - Ventilador: Ventilador de 2 pines, se encuentra comunmente en computadoras de escritorio
  BeagleBone Black V3: BeagleBone Black rev. A5B
  H-Bridge with L298N v2: h-bridge
